// Logisim project 6502.circ as structural Verilog: 6 circuits, main circuit ALU
module ALU (
  input  carry_in,
  input  [7:0] op1,
  input  [7:0] op2,
  input  [2:0] operation,
  output carry_out,
  output v,
  output [7:0] Result,
  output z,
  output n
);

  wire xnor_1_out, xor_1_out;
  wire [7:0] adder_1_out;

  Adder adder_1 (.a(op1), .b(op2), .out(adder_1_out), .cin(carry_in), .cout(carry_out));
  Multiplexer #(.select(3), .width(8), .enable("false")) multiplexer_1 (
    .in0(adder_1_out), .in1(op1), .in2(op2), .out({n, Result[6:0]}), .sel(operation));  // open: in3, in4, in5, in6, in7
  xnor xnor_1 (xnor_1_out, op1[7], op2[7]);
  xor xor_1 (xor_1_out, op1[7], n);
  and and_1 (v, xnor_1_out, xor_1_out);
  Comparator comparator_1 (.a({n, Result[6:0]}), .b({8{1'b0}}), .eq(z));  // open: gt, lt

  assign Result[7] = n;
endmodule

module main (
  input  in_1,
  input  in_2,
  input  in_3,
  input  sb_db,
  input  in_5,
  input  in_6,
  input  s_sb,
  input  in_8,
  input  db_sb,
  input  in_10,
  input  in_11,
  input  sb_adh,
  input  in_13,
  input  s_adl,
  input  in_15,
  input  adh_sb,
  input  in_17,
  input  [2:0] in_18,
  input  in_19,
  input  add_adl,
  input  in_21,
  input  [1:0] in_22,
  input  in_23,
  input  add_sb,
  input  in_25,
  input  in_26,
  input  in_27,
  input  in_28,
  input  in_29,
  input  in_30,
  input  dl_adh,
  input  in_32,
  input  dl_adl,
  input  in_34,
  input  in_35,
  input  in_36
);

  wire c, clk, co, multiplexer_3_out;
  wire [7:0] AC_q, ADD_q, ADH, ADL, AI_q, alu_1_result, BI_q, DB, DL_q, multiplexer_1_out, multiplexer_2_out,
       multiplexer_5_out, not_1_out, PCL_q, PCL_q_2, S_q, SB, X_q, Y_q;
  wire [15:0] adder_1_out, ADDR, multiplexer_4_out;

  assign DB = sb_db ? SB : 8'bz;  // Controlled_Buffer controlled_buffer_1
  assign SB = db_sb ? DB : 8'bz;  // Controlled_Buffer controlled_buffer_2
  assign not_1_out = ~DB;  // NOT_Gate not_1, 8 bits wide
  Multiplexer #(.select(2), .width(8), .enable("false")) multiplexer_1 (
    .in0(ADL), .in1(not_1_out), .in2(DB), .out(multiplexer_1_out), .sel(in_22));  // open: in3
  Multiplexer #(.width(8), .enable("false")) multiplexer_2 (
    .in0({8{1'b0}}), .in1(SB), .out(multiplexer_2_out), .sel(in_28));
  Register S (.D(SB), .en(in_10), .Q(S_q), .clk(clk));  // open: clr
  Multiplexer #(.enable("false")) multiplexer_3 (.in0(c), .in1(1'b1), .out(multiplexer_3_out), .sel(in_15));
  Register BI (.D(multiplexer_1_out), .en(in_21), .Q(BI_q), .clk(clk));  // open: clr
  Register AI (.D(multiplexer_2_out), .en(in_27), .Q(AI_q), .clk(clk));  // open: clr
  assign SB = s_sb ? S_q : 8'bz;  // Controlled_Buffer controlled_buffer_3
  assign ADL = s_adl ? S_q : 8'bz;  // Controlled_Buffer controlled_buffer_4
  ALU alu_1 (
    .op1(AI_q), .op2(BI_q), .Result(alu_1_result), .carry_out(co), .operation(in_18),
    .carry_in(multiplexer_3_out));  // open: v, z, n
  assign ADL = add_adl ? ADD_q : 8'bz;  // Controlled_Buffer controlled_buffer_5
  Register ADD (.D(alu_1_result), .en(in_23), .Q(ADD_q), .clk(clk));  // open: clr
  assign DB = in_29 ? AC_q : 8'bz;  // Controlled_Buffer controlled_buffer_6
  Register AC (.D(SB), .en(in_34), .Q(AC_q), .clk(clk));  // open: clr
  assign ADH = sb_adh ? SB : 8'bz;  // Controlled_Buffer controlled_buffer_7
  assign SB = add_sb ? ADD_q : 8'bz;  // Controlled_Buffer controlled_buffer_8
  assign SB = adh_sb ? ADH : 8'bz;  // Controlled_Buffer controlled_buffer_9
  Multiplexer #(.width(16), .enable("false")) multiplexer_4 (
    .in0({ADH, ADL}), .in1(adder_1_out), .out(multiplexer_4_out), .sel(in_2));
  Adder #(.width(16)) adder_1 (.a(16'h1), .b({ADH, ADL}), .out(adder_1_out));  // open: cin, cout
  assign SB = in_8 ? PCL_q_2 : 8'bz;  // Controlled_Buffer controlled_buffer_10
  assign SB = in_13 ? PCL_q : 8'bz;  // Controlled_Buffer controlled_buffer_11
  assign SB = in_19 ? X_q : 8'bz;  // Controlled_Buffer controlled_buffer_12
  Register X (.D(SB), .en(in_25), .Q(X_q), .clk(clk));  // open: clr
  assign SB = in_30 ? Y_q : 8'bz;  // Controlled_Buffer controlled_buffer_13
  Register Y (.D(SB), .en(in_35), .Q(Y_q), .clk(clk));  // open: clr
  Register #(.width(16)) PCL (.D(multiplexer_4_out), .en(in_3), .Q({PCL_q_2, PCL_q}), .clk(clk));  // open: clr
  Button button_1 (.out(clk));
  assign {ADH, ADL} = in_1 ? {PCL_q_2, PCL_q} : 16'bz;  // Controlled_Buffer controlled_buffer_14
  Register #(.width(1)) u_c (.D(co), .en(in_36), .Q(c), .clk(clk));  // open: clr
  RAM #(.addrWidth(16)) ram_1 (.addr(ADDR), .data(DB), .ld(in_26));  // open: sel, clk, clr
  Multiplexer #(.width(8), .enable("false")) multiplexer_5 (
    .in0(ADH), .in1({8{1'b0}}), .out(multiplexer_5_out), .sel(in_5));
  Register DL (.D(DB), .en(in_32), .Q(DL_q), .clk(clk));  // open: clr
  Register ABH (.D(multiplexer_5_out), .en(in_6), .Q(ADDR[15:8]), .clk(clk));  // open: clr
  Register ABL (.D(ADL), .en(in_11), .Q(ADDR[7:0]), .clk(clk));  // open: clr
  Register IR (.D(DB), .en(in_17), .clk(clk));  // open: Q, clr
  assign ADH = dl_adh ? DL_q : 8'bz;  // Controlled_Buffer controlled_buffer_15
  assign ADL = dl_adl ? DL_q : 8'bz;  // Controlled_Buffer controlled_buffer_16
endmodule

module datapath_v2 (
  input  in_1,
  input  in_2,
  input  in_3,
  input  sb_db,
  input  in_5,
  input  in_6,
  input  s_sb,
  input  in_8,
  input  db_sb,
  input  in_10,
  input  in_11,
  input  sb_adh,
  input  in_13,
  input  s_adl,
  input  in_15,
  input  adh_sb,
  input  in_17,
  input  [2:0] in_18,
  input  in_19,
  input  alu_adl,
  input  in_21,
  input  [1:0] in_22,
  input  alu_sb,
  input  in_24,
  input  in_25,
  input  in_26,
  input  in_27,
  input  in_28,
  input  db_adh,
  input  [1:0] in_30,
  input  db_adl,
  input  in_32,
  input  in_33,
  input  in_34
);

  wire c, clk, co, multiplexer_3_out;
  wire [7:0] AC, ADH, ADL, AI_q, alu_1_result, BI_q, DB, multiplexer_1_out, multiplexer_2_out,
       multiplexer_5_out, not_1_out, PC_q, PC_q_2, S_q, SB, X_q, Y_q;
  wire [15:0] adder_1_out, ADDR, multiplexer_4_out;

  assign DB = sb_db ? SB : 8'bz;  // Controlled_Buffer controlled_buffer_1
  assign not_1_out = ~DB;  // NOT_Gate not_1, 8 bits wide
  assign SB = db_sb ? DB : 8'bz;  // Controlled_Buffer controlled_buffer_2
  Multiplexer #(.select(2), .width(8), .enable("false")) multiplexer_1 (
    .in0(ADL), .in1(not_1_out), .in2(DB), .out(multiplexer_1_out), .sel(in_22));  // open: in3
  Multiplexer #(.select(2), .width(8), .enable("false")) multiplexer_2 (
    .in0(AC), .in1(SB), .in2({8{1'b0}}), .out(multiplexer_2_out), .sel(in_30));  // open: in3
  Register S (.D(SB), .en(in_10), .Q(S_q), .clk(clk));  // open: clr
  Multiplexer #(.enable("false")) multiplexer_3 (.in0(c), .in1(1'b1), .out(multiplexer_3_out), .sel(in_15));
  Register BI (.D(multiplexer_1_out), .en(in_21), .Q(BI_q), .clk(clk));  // open: clr
  Register AI (.D(multiplexer_2_out), .en(in_26), .Q(AI_q), .clk(clk));  // open: clr
  assign SB = s_sb ? S_q : 8'bz;  // Controlled_Buffer controlled_buffer_3
  assign ADL = s_adl ? S_q : 8'bz;  // Controlled_Buffer controlled_buffer_4
  ALU alu_1 (
    .op1(AI_q), .op2(BI_q), .Result(alu_1_result), .carry_out(co), .operation(in_18),
    .carry_in(multiplexer_3_out));  // open: v, z, n
  assign ADL = alu_adl ? alu_1_result : 8'bz;  // Controlled_Buffer controlled_buffer_5
  assign DB = in_27 ? AC : 8'bz;  // Controlled_Buffer controlled_buffer_6
  Register u_AC (.D(SB), .en(in_32), .Q(AC), .clk(clk));  // open: clr
  assign ADH = sb_adh ? SB : 8'bz;  // Controlled_Buffer controlled_buffer_7
  assign SB = alu_sb ? alu_1_result : 8'bz;  // Controlled_Buffer controlled_buffer_8
  assign SB = adh_sb ? ADH : 8'bz;  // Controlled_Buffer controlled_buffer_9
  Multiplexer #(.width(16), .enable("false")) multiplexer_4 (
    .in0({ADH, ADL}), .in1(adder_1_out), .out(multiplexer_4_out), .sel(in_2));
  Adder #(.width(16)) adder_1 (.a(16'h1), .b({ADH, ADL}), .out(adder_1_out));  // open: cin, cout
  assign SB = in_8 ? PC_q_2 : 8'bz;  // Controlled_Buffer controlled_buffer_10
  assign SB = in_13 ? PC_q : 8'bz;  // Controlled_Buffer controlled_buffer_11
  assign SB = in_19 ? X_q : 8'bz;  // Controlled_Buffer controlled_buffer_12
  Register X (.D(SB), .en(in_24), .Q(X_q), .clk(clk));  // open: clr
  assign SB = in_28 ? Y_q : 8'bz;  // Controlled_Buffer controlled_buffer_13
  Register Y (.D(SB), .en(in_33), .Q(Y_q), .clk(clk));  // open: clr
  Register #(.width(16)) PC (.D(multiplexer_4_out), .en(in_3), .Q({PC_q_2, PC_q}), .clk(clk));  // open: clr
  Button button_1 (.out(clk));
  assign {ADH, ADL} = in_1 ? {PC_q_2, PC_q} : 16'bz;  // Controlled_Buffer controlled_buffer_14
  Register #(.width(1)) u_c (.D(co), .en(in_34), .Q(c), .clk(clk));  // open: clr
  RAM #(.addrWidth(16)) ram_1 (.addr(ADDR), .data(DB), .ld(in_25));  // open: sel, clk, clr
  Multiplexer #(.width(8), .enable("false")) multiplexer_5 (
    .in0(ADH), .in1({8{1'b0}}), .out(multiplexer_5_out), .sel(in_5));
  Register ABH (.D(multiplexer_5_out), .en(in_6), .Q(ADDR[15:8]), .clk(clk));  // open: clr
  Register ABL (.D(ADL), .en(in_11), .Q(ADDR[7:0]), .clk(clk));  // open: clr
  Register IR (.D(DB), .en(in_17), .clk(clk));  // open: Q, clr
  assign ADH = db_adh ? DB : 8'bz;  // Controlled_Buffer controlled_buffer_15
  assign ADL = db_adl ? DB : 8'bz;  // Controlled_Buffer controlled_buffer_16
endmodule

module datapath_v3 (
  input  in_1,
  input  in_2,
  input  [1:0] in_3,
  input  sb_db,
  input  in_5,
  input  in_6,
  input  s_sb,
  input  db_sb,
  input  in_9,
  input  in_10,
  input  in_11,
  input  sb_adh,
  input  s_adl,
  input  pch_db,
  input  pcl_db,
  input  [1:0] in_16,
  input  adh_sb,
  input  x_sb,
  input  in_19,
  input  [2:0] in_20,
  input  alu_adl,
  input  in_22,
  input  in_23,
  input  in_24,
  input  alu_sb,
  input  in_26,
  input  in_27,
  input  ac_db,
  input  ac_sb,
  input  y_sb,
  input  db_adh,
  input  [1:0] in_32,
  input  db_adl,
  input  in_34,
  input  in_35,
  input  set_c,
  input  wrc,
  input  cl_c
);

  wire c, clk, co, hc, multiplexer_1_out;
  wire [7:0] AC, ADH, ADL, AI_q, alu_1_result, BI_q, DB, multiplexer_2_out, multiplexer_3_out,
       multiplexer_5_out, not_1_out, S_q, SB, X_q, Y_q;
  wire [15:0] adder_1_out, ADDR, multiplexer_4_out, PCL_q;

  assign DB = sb_db ? SB : 8'bz;  // Controlled_Buffer controlled_buffer_1
  assign not_1_out = ~DB;  // NOT_Gate not_1, 8 bits wide
  assign SB = db_sb ? DB : 8'bz;  // Controlled_Buffer controlled_buffer_2
  Multiplexer #(.select(2), .enable("false")) multiplexer_1 (
    .in0(1'b0), .in1(1'b1), .in2(c), .in3(hc), .out(multiplexer_1_out), .sel(in_16));
  Multiplexer #(.width(8), .enable("false")) multiplexer_2 (
    .in0(DB), .in1(not_1_out), .out(multiplexer_2_out), .sel(in_23));
  Multiplexer #(.select(2), .width(8), .enable("false")) multiplexer_3 (
    .in0(ADL), .in1(SB), .in2({8{1'b0}}), .out(multiplexer_3_out), .sel(in_32));  // open: in3
  Register S (.D(SB), .en(in_10), .Q(S_q), .clk(clk));  // open: clr
  Register BI (.D(multiplexer_2_out), .en(in_22), .Q(BI_q), .clk(clk));  // open: clr
  Register AI (.D(multiplexer_3_out), .en(in_27), .Q(AI_q), .clk(clk));  // open: clr
  assign SB = s_sb ? S_q : 8'bz;  // Controlled_Buffer controlled_buffer_3
  assign ADL = s_adl ? S_q : 8'bz;  // Controlled_Buffer controlled_buffer_4
  ALU alu_1 (
    .op1(AI_q), .op2(BI_q), .Result(alu_1_result), .carry_out(co), .operation(in_20),
    .carry_in(multiplexer_1_out));  // open: v, z, n
  assign ADL = alu_adl ? alu_1_result : 8'bz;  // Controlled_Buffer controlled_buffer_5
  assign DB = ac_db ? AC : 8'bz;  // Controlled_Buffer controlled_buffer_6
  Register u_AC (.D(SB), .en(in_34), .Q(AC), .clk(clk));  // open: clr
  assign ADH = sb_adh ? SB : 8'bz;  // Controlled_Buffer controlled_buffer_7
  assign SB = adh_sb ? ADH : 8'bz;  // Controlled_Buffer controlled_buffer_8
  assign SB = alu_sb ? alu_1_result : 8'bz;  // Controlled_Buffer controlled_buffer_9
  assign SB = ac_sb ? AC : 8'bz;  // Controlled_Buffer controlled_buffer_10
  Adder #(.width(16)) adder_1 (.a(PCL_q), .b(16'h1), .out(adder_1_out));  // open: cin, cout
  assign SB = x_sb ? X_q : 8'bz;  // Controlled_Buffer controlled_buffer_11
  assign SB = y_sb ? Y_q : 8'bz;  // Controlled_Buffer controlled_buffer_12
  Multiplexer #(.width(16), .enable("false")) multiplexer_4 (
    .in0(adder_1_out), .in1({ADH, ADL}), .out(multiplexer_4_out), .sel(in_5));
  Register X (.D(SB), .en(in_24), .Q(X_q), .clk(clk));  // open: clr
  Register Y (.D(SB), .en(in_35), .Q(Y_q), .clk(clk));  // open: clr
  Button button_1 (.out(clk));
  Register PCH (.D(multiplexer_4_out[15:8]), .en(in_1), .Q(PCL_q[15:8]), .clk(clk));  // open: clr
  Register PCL (.D(multiplexer_4_out[7:0]), .en(in_9), .Q(PCL_q[7:0]), .clk(clk));  // open: clr
  assign DB = pch_db ? PCL_q[15:8] : 8'bz;  // Controlled_Buffer controlled_buffer_13
  D_Flip_Flop u_c (.clk(clk), .D(co), .Q(c), .preset(set_c), .en(wrc), .reset(cl_c));  // open: Qn
  assign ADH = in_2 ? PCL_q[15:8] : 8'bz;  // Controlled_Buffer controlled_buffer_14
  assign ADL = in_2 ? PCL_q[7:0] : 8'bz;  // Controlled_Buffer controlled_buffer_15
  assign DB = pcl_db ? PCL_q[7:0] : 8'bz;  // Controlled_Buffer controlled_buffer_16
  RAM #(.addrWidth(16)) ram_1 (.addr(ADDR), .data(DB), .ld(in_26));  // open: sel, clk, clr
  Register #(.width(1)) u_hc (.D(co), .Q(hc), .clk(clk));  // open: en, clr
  Multiplexer #(.select(2), .width(8), .enable("false")) multiplexer_5 (
    .in0(ADH), .in2({8{1'b0}}), .in3(8'h1), .out(multiplexer_5_out), .sel(in_3));  // open: in1
  Register ABH (.D(multiplexer_5_out), .en(in_6), .Q(ADDR[15:8]), .clk(clk));  // open: clr
  Register ABL (.D(ADL), .en(in_11), .Q(ADDR[7:0]), .clk(clk));  // open: clr
  Register IR (.D(DB), .en(in_19), .clk(clk));  // open: Q, clr
  assign ADH = db_adh ? DB : 8'bz;  // Controlled_Buffer controlled_buffer_17
  assign ADL = db_adl ? DB : 8'bz;  // Controlled_Buffer controlled_buffer_18
endmodule

module datapath_v4 (
  input  s_adl,
  input  mux_s,
  input  in_3,
  input  in_4,
  input  pc_ad,
  input  [1:0] mux_abh,
  input  sb_db,
  input  mux_pc,
  input  in_9,
  input  s_sb,
  input  db_sb,
  input  in_12,
  input  in_13,
  input  [1:0] mux_carry,
  input  sb_adh,
  input  x_sb,
  input  pch_db,
  input  pcl_db,
  input  adh_sb,
  input  in_20,
  input  [2:0] in_21,
  input  alu_adl,
  input  in_23,
  input  in_24,
  input  mux_bi,
  input  alu_sb,
  input  y_sb,
  input  in_28,
  input  in_29,
  input  in_30,
  input  [1:0] mux_ai,
  input  ac_db,
  input  ac_sb,
  input  db_adh,
  input  in_35,
  input  db_adl,
  input  in_37,
  input  set_c,
  input  wrc,
  input  cl_c
);

  wire c, clk, co, hc, multiplexer_4_out, not_2_out;
  wire [7:0] AC_q, ADH, ADL, AI_q, alu_1_result, BI_q, DB, multiplexer_1_out, multiplexer_2_out,
       multiplexer_3_out, multiplexer_6_out, not_1_out, S_q, SB, subtractor_1_out, X_q, Y_q;
  wire [15:0] adder_1_out, ADDR, multiplexer_5_out, PCL_q;

  assign DB = sb_db ? SB : 8'bz;  // Controlled_Buffer controlled_buffer_1
  assign not_1_out = ~DB;  // NOT_Gate not_1, 8 bits wide
  Subtractor subtractor_1 (.a(S_q), .b(8'h1), .out(subtractor_1_out));  // open: bin, bout
  assign SB = db_sb ? DB : 8'bz;  // Controlled_Buffer controlled_buffer_2
  not not_2 (not_2_out, c);
  Multiplexer #(.width(8), .enable("false")) multiplexer_1 (
    .in0(DB), .in1(not_1_out), .out(multiplexer_1_out), .sel(mux_bi));
  Multiplexer #(.select(2), .width(8), .enable("false")) multiplexer_2 (
    .in0(ADL), .in1(SB), .in2({8{1'b0}}), .out(multiplexer_2_out), .sel(mux_ai));  // open: in3
  Multiplexer #(.width(8), .enable("false")) multiplexer_3 (
    .in0(subtractor_1_out), .in1(SB), .out(multiplexer_3_out), .sel(mux_s));
  Multiplexer #(.select(2), .enable("false")) multiplexer_4 (
    .in0(1'b1), .in1(not_2_out), .in2(c), .in3(hc), .out(multiplexer_4_out), .sel(mux_carry));
  Register BI (.D(multiplexer_1_out), .en(in_24), .Q(BI_q), .clk(clk));  // open: clr
  Register AI (.D(multiplexer_2_out), .en(in_30), .Q(AI_q), .clk(clk));  // open: clr
  Register S (.D(multiplexer_3_out), .en(in_3), .Q(S_q), .clk(clk));  // open: clr
  assign ADL = s_adl ? S_q : 8'bz;  // Controlled_Buffer controlled_buffer_3
  assign SB = s_sb ? S_q : 8'bz;  // Controlled_Buffer controlled_buffer_4
  ALU alu_1 (
    .op1(AI_q), .op2(BI_q), .Result(alu_1_result), .carry_out(co), .operation(in_21),
    .carry_in(multiplexer_4_out));  // open: v, z, n
  assign ADL = alu_adl ? alu_1_result : 8'bz;  // Controlled_Buffer controlled_buffer_5
  assign DB = ac_db ? AC_q : 8'bz;  // Controlled_Buffer controlled_buffer_6
  Register AC (.D(SB), .en(in_37), .Q(AC_q), .clk(clk));  // open: clr
  assign ADH = sb_adh ? SB : 8'bz;  // Controlled_Buffer controlled_buffer_7
  assign SB = adh_sb ? ADH : 8'bz;  // Controlled_Buffer controlled_buffer_8
  assign SB = alu_sb ? alu_1_result : 8'bz;  // Controlled_Buffer controlled_buffer_9
  assign SB = ac_sb ? AC_q : 8'bz;  // Controlled_Buffer controlled_buffer_10
  Adder #(.width(16)) adder_1 (.a(PCL_q), .b(16'h1), .out(adder_1_out));  // open: cin, cout
  assign SB = x_sb ? X_q : 8'bz;  // Controlled_Buffer controlled_buffer_11
  assign SB = y_sb ? Y_q : 8'bz;  // Controlled_Buffer controlled_buffer_12
  Multiplexer #(.width(16), .enable("false")) multiplexer_5 (
    .in0(adder_1_out), .in1({ADH, ADL}), .out(multiplexer_5_out), .sel(mux_pc));
  Register X (.D(SB), .en(in_23), .Q(X_q), .clk(clk));  // open: clr
  Register Y (.D(SB), .en(in_35), .Q(Y_q), .clk(clk));  // open: clr
  Button button_1 (.out(clk));
  Register PCH (.D(multiplexer_5_out[15:8]), .en(in_4), .Q(PCL_q[15:8]), .clk(clk));  // open: clr
  Register PCL (.D(multiplexer_5_out[7:0]), .en(in_12), .Q(PCL_q[7:0]), .clk(clk));  // open: clr
  assign DB = pch_db ? PCL_q[15:8] : 8'bz;  // Controlled_Buffer controlled_buffer_13
  D_Flip_Flop u_c (.clk(clk), .D(co), .Q(c), .preset(set_c), .en(wrc), .reset(cl_c));  // open: Qn
  assign ADH = pc_ad ? PCL_q[15:8] : 8'bz;  // Controlled_Buffer controlled_buffer_14
  assign ADL = pc_ad ? PCL_q[7:0] : 8'bz;  // Controlled_Buffer controlled_buffer_15
  assign DB = pcl_db ? PCL_q[7:0] : 8'bz;  // Controlled_Buffer controlled_buffer_16
  RAM #(.addrWidth(16)) ram_1 (.addr(ADDR), .data(DB), .sel(in_28), .clk(clk), .ld(in_29));  // open: clr
  Register #(.width(1)) u_hc (.D(co), .Q(hc), .clk(clk));  // open: en, clr
  Multiplexer #(.select(2), .width(8), .enable("false")) multiplexer_6 (
    .in0(ADH), .in1({8{1'b0}}), .in2(8'h1), .out(multiplexer_6_out), .sel(mux_abh));  // open: in3
  Register ABH (.D(multiplexer_6_out), .en(in_9), .Q(ADDR[15:8]), .clk(clk));  // open: clr
  Register ABL (.D(ADL), .en(in_13), .Q(ADDR[7:0]), .clk(clk));  // open: clr
  Register IR (.D(DB), .en(in_20), .clk(clk));  // open: Q, clr
  assign ADH = db_adh ? DB : 8'bz;  // Controlled_Buffer controlled_buffer_17
  assign ADL = db_adl ? DB : 8'bz;  // Controlled_Buffer controlled_buffer_18
endmodule

module datapath_v5 (
  input  s_adl,
  input  mux_s,
  input  in_3,
  input  in_4,
  input  pc_ad,
  input  [1:0] mux_abh,
  input  sb_db,
  input  mux_pc,
  input  in_9,
  input  s_sb,
  input  db_sb,
  input  in_12,
  input  in_13,
  input  [1:0] mux_carry,
  input  sb_adh,
  input  x_sb,
  input  pch_db,
  input  pcl_db,
  input  adh_sb,
  input  in_20,
  input  [2:0] in_21,
  input  alu_adl,
  input  in_23,
  input  in_24,
  input  mux_bi,
  input  alu_sb,
  input  y_sb,
  input  in_28,
  input  in_29,
  input  in_30,
  input  [1:0] mux_ai,
  input  ac_db,
  input  ac_sb,
  input  db_adh,
  input  in_35,
  input  db_adl,
  input  in_37,
  input  set_c,
  input  wrc,
  input  cl_c,
  input  set_v,
  input  wrv,
  input  cl_v,
  input  set_n,
  input  wrn,
  input  cl_n,
  input  set_z,
  input  wrz,
  input  cl_z
);

  wire c, clk, co, hc, multiplexer_4_out, n, no, not_2_out, v, vo, z, zo;
  wire [7:0] AC_q, ADH, ADL, AI_q, alu_1_result, BI_q, DB, multiplexer_1_out, multiplexer_2_out,
       multiplexer_3_out, multiplexer_6_out, not_1_out, S_q, SB, subtractor_1_out, X_q, Y_q;
  wire [15:0] adder_1_out, ADDR, multiplexer_5_out, PCL_q;

  assign DB = sb_db ? SB : 8'bz;  // Controlled_Buffer controlled_buffer_1
  assign not_1_out = ~DB;  // NOT_Gate not_1, 8 bits wide
  Subtractor subtractor_1 (.a(S_q), .b(8'h1), .out(subtractor_1_out));  // open: bin, bout
  assign SB = db_sb ? DB : 8'bz;  // Controlled_Buffer controlled_buffer_2
  not not_2 (not_2_out, c);
  Multiplexer #(.width(8), .enable("false")) multiplexer_1 (
    .in0(DB), .in1(not_1_out), .out(multiplexer_1_out), .sel(mux_bi));
  Multiplexer #(.select(2), .width(8), .enable("false")) multiplexer_2 (
    .in0(ADL), .in1(SB), .in2({8{1'b0}}), .out(multiplexer_2_out), .sel(mux_ai));  // open: in3
  Multiplexer #(.width(8), .enable("false")) multiplexer_3 (
    .in0(subtractor_1_out), .in1(SB), .out(multiplexer_3_out), .sel(mux_s));
  Multiplexer #(.select(2), .enable("false")) multiplexer_4 (
    .in0(1'b1), .in1(not_2_out), .in2(c), .in3(hc), .out(multiplexer_4_out), .sel(mux_carry));
  Register BI (.D(multiplexer_1_out), .en(in_24), .Q(BI_q), .clk(clk));  // open: clr
  Register AI (.D(multiplexer_2_out), .en(in_30), .Q(AI_q), .clk(clk));  // open: clr
  Register S (.D(multiplexer_3_out), .en(in_3), .Q(S_q), .clk(clk));  // open: clr
  assign ADL = s_adl ? S_q : 8'bz;  // Controlled_Buffer controlled_buffer_3
  assign SB = s_sb ? S_q : 8'bz;  // Controlled_Buffer controlled_buffer_4
  ALU alu_1 (
    .op1(AI_q), .op2(BI_q), .Result(alu_1_result), .carry_out(co), .operation(in_21),
    .carry_in(multiplexer_4_out), .v(vo), .z(zo), .n(no));
  assign ADL = alu_adl ? alu_1_result : 8'bz;  // Controlled_Buffer controlled_buffer_5
  assign DB = ac_db ? AC_q : 8'bz;  // Controlled_Buffer controlled_buffer_6
  Register AC (.D(SB), .en(in_37), .Q(AC_q), .clk(clk));  // open: clr
  assign ADH = sb_adh ? SB : 8'bz;  // Controlled_Buffer controlled_buffer_7
  assign SB = adh_sb ? ADH : 8'bz;  // Controlled_Buffer controlled_buffer_8
  assign SB = alu_sb ? alu_1_result : 8'bz;  // Controlled_Buffer controlled_buffer_9
  assign SB = ac_sb ? AC_q : 8'bz;  // Controlled_Buffer controlled_buffer_10
  Adder #(.width(16)) adder_1 (.a(PCL_q), .b(16'h1), .out(adder_1_out));  // open: cin, cout
  assign SB = x_sb ? X_q : 8'bz;  // Controlled_Buffer controlled_buffer_11
  assign SB = y_sb ? Y_q : 8'bz;  // Controlled_Buffer controlled_buffer_12
  Multiplexer #(.width(16), .enable("false")) multiplexer_5 (
    .in0(adder_1_out), .in1({ADH, ADL}), .out(multiplexer_5_out), .sel(mux_pc));
  Register X (.D(SB), .en(in_23), .Q(X_q), .clk(clk));  // open: clr
  Register Y (.D(SB), .en(in_35), .Q(Y_q), .clk(clk));  // open: clr
  D_Flip_Flop u_v (.clk(clk), .D(vo), .Q(v), .preset(set_v), .en(wrv), .reset(cl_v));  // open: Qn
  Button button_1 (.out(clk));
  Register PCH (.D(multiplexer_5_out[15:8]), .en(in_4), .Q(PCL_q[15:8]), .clk(clk));  // open: clr
  Register PCL (.D(multiplexer_5_out[7:0]), .en(in_12), .Q(PCL_q[7:0]), .clk(clk));  // open: clr
  assign DB = pch_db ? PCL_q[15:8] : 8'bz;  // Controlled_Buffer controlled_buffer_13
  D_Flip_Flop u_c (.clk(clk), .D(co), .Q(c), .preset(set_c), .en(wrc), .reset(cl_c));  // open: Qn
  D_Flip_Flop u_n (.clk(clk), .D(no), .Q(n), .preset(set_n), .en(wrn), .reset(cl_n));  // open: Qn
  assign ADH = pc_ad ? PCL_q[15:8] : 8'bz;  // Controlled_Buffer controlled_buffer_14
  assign ADL = pc_ad ? PCL_q[7:0] : 8'bz;  // Controlled_Buffer controlled_buffer_15
  assign DB = pcl_db ? PCL_q[7:0] : 8'bz;  // Controlled_Buffer controlled_buffer_16
  RAM #(.addrWidth(16)) ram_1 (.addr(ADDR), .data(DB), .sel(in_28), .clk(clk), .ld(in_29));  // open: clr
  Register #(.width(1)) u_hc (.D(co), .Q(hc), .clk(clk));  // open: en, clr
  D_Flip_Flop u_z (.clk(clk), .D(zo), .Q(z), .preset(set_z), .en(wrz), .reset(cl_z));  // open: Qn
  Multiplexer #(.select(2), .width(8), .enable("false")) multiplexer_6 (
    .in0(ADH), .in1({8{1'b0}}), .in2(8'h1), .out(multiplexer_6_out), .sel(mux_abh));  // open: in3
  Register ABH (.D(multiplexer_6_out), .en(in_9), .Q(ADDR[15:8]), .clk(clk));  // open: clr
  Register ABL (.D(ADL), .en(in_13), .Q(ADDR[7:0]), .clk(clk));  // open: clr
  Register IR (.D(DB), .en(in_20), .clk(clk));  // open: Q, clr
  assign ADH = db_adh ? DB : 8'bz;  // Controlled_Buffer controlled_buffer_17
  assign ADL = db_adl ? DB : 8'bz;  // Controlled_Buffer controlled_buffer_18

  // Notes on the sheet:
  //   Processor Status Register (P)
endmodule
